// Logisim project projeto_1.circ as structural Verilog: 5 circuits, main circuit adder_8bits
module adder_8bits (
  input  [7:0] A,
  input  [7:0] B,
  output [7:0] S
);

  wire full_adder_2_cin_2, full_adder_3_cin_2, full_adder_4_cin_2, full_adder_5_cin_2, full_adder_6_cin_2,
       full_adder_7_cin_2, full_adder_8_cin_2;

  full_adder full_adder_1 (.A(A[7]), .B(B[7]), .Cin(full_adder_2_cin_2), .Soma(S[7]));  // open: Cin_2
  full_adder full_adder_2 (.A(A[6]), .B(B[6]), .Cin(full_adder_3_cin_2), .Soma(S[6]), .Cin_2(full_adder_2_cin_2));
  full_adder full_adder_3 (.A(A[5]), .B(B[5]), .Cin(full_adder_4_cin_2), .Soma(S[5]), .Cin_2(full_adder_3_cin_2));
  full_adder full_adder_4 (.A(A[4]), .B(B[4]), .Cin(full_adder_5_cin_2), .Soma(S[4]), .Cin_2(full_adder_4_cin_2));
  full_adder full_adder_5 (.A(A[3]), .B(B[3]), .Cin(full_adder_6_cin_2), .Soma(S[3]), .Cin_2(full_adder_5_cin_2));
  full_adder full_adder_6 (.A(A[2]), .B(B[2]), .Cin(full_adder_7_cin_2), .Soma(S[2]), .Cin_2(full_adder_6_cin_2));
  full_adder full_adder_7 (.A(A[1]), .B(B[1]), .Cin(full_adder_8_cin_2), .Soma(S[1]), .Cin_2(full_adder_7_cin_2));
  full_adder full_adder_8 (.A(A[0]), .B(B[0]), .Cin(1'b0), .Soma(S[0]), .Cin_2(full_adder_8_cin_2));

  // Notes on the sheet:
  //   SOMADOR 8Bits
endmodule

module subtractor_8bits (
  input  [7:0] A,
  input  [7:0] B,
  output [7:0] S
);

  wire full_subtractor_2_bout, full_subtractor_3_bout, full_subtractor_4_bout, full_subtractor_5_bout,
       full_subtractor_6_bout, full_subtractor_7_bout, full_subtractor_8_bout;

  full_subtractor full_subtractor_1 (.A(A[7]), .B(B[7]), .Bin(full_subtractor_2_bout), .S(S[7]));  // open: Bout
  full_subtractor full_subtractor_2 (
    .A(A[6]), .B(B[6]), .Bin(full_subtractor_3_bout), .S(S[6]), .Bout(full_subtractor_2_bout));
  full_subtractor full_subtractor_3 (
    .A(A[5]), .B(B[5]), .Bin(full_subtractor_4_bout), .S(S[5]), .Bout(full_subtractor_3_bout));
  full_subtractor full_subtractor_4 (
    .A(A[4]), .B(B[4]), .Bin(full_subtractor_5_bout), .S(S[4]), .Bout(full_subtractor_4_bout));
  full_subtractor full_subtractor_5 (
    .A(A[3]), .B(B[3]), .Bin(full_subtractor_6_bout), .S(S[3]), .Bout(full_subtractor_5_bout));
  full_subtractor full_subtractor_6 (
    .A(A[2]), .B(B[2]), .Bin(full_subtractor_7_bout), .S(S[2]), .Bout(full_subtractor_6_bout));
  full_subtractor full_subtractor_7 (
    .A(A[1]), .B(B[1]), .Bin(full_subtractor_8_bout), .S(S[1]), .Bout(full_subtractor_7_bout));
  full_subtractor full_subtractor_8 (.A(A[0]), .B(B[0]), .Bin(1'b0), .S(S[0]), .Bout(full_subtractor_8_bout));

  // Notes on the sheet:
  //   SUBTRATOR 8Bits
endmodule

module desloc_left (
  input  [7:0] B,
  input  Clk,
  input  Set,
  output [7:0] S
);

  wire multiplexer_1_out, multiplexer_2_out, multiplexer_3_out, multiplexer_4_out, multiplexer_5_out,
       multiplexer_6_out, multiplexer_7_out, multiplexer_8_out;

  Multiplexer #(.enable("false")) multiplexer_1 (.in0(1'b0), .in1(B[0]), .out(multiplexer_1_out), .sel(Set));
  D_Flip_Flop d_ff_1 (.clk(Clk), .D(multiplexer_1_out), .Q(S[0]), .en(1'b1));  // open: Qn, preset, reset
  Multiplexer #(.enable("false")) multiplexer_2 (.in0(S[0]), .in1(B[1]), .out(multiplexer_2_out), .sel(Set));
  D_Flip_Flop d_ff_2 (.clk(Clk), .D(multiplexer_2_out), .Q(S[1]), .en(1'b1));  // open: Qn, preset, reset
  Multiplexer #(.enable("false")) multiplexer_3 (.in0(S[1]), .in1(B[2]), .out(multiplexer_3_out), .sel(Set));
  D_Flip_Flop d_ff_3 (.clk(Clk), .D(multiplexer_3_out), .Q(S[2]), .en(1'b1));  // open: Qn, preset, reset
  Multiplexer #(.enable("false")) multiplexer_4 (.in0(S[2]), .in1(B[3]), .out(multiplexer_4_out), .sel(Set));
  D_Flip_Flop d_ff_4 (.clk(Clk), .D(multiplexer_4_out), .Q(S[3]), .en(1'b1));  // open: Qn, preset, reset
  Multiplexer #(.enable("false")) multiplexer_5 (.in0(S[3]), .in1(B[4]), .out(multiplexer_5_out), .sel(Set));
  D_Flip_Flop d_ff_5 (.clk(Clk), .D(multiplexer_5_out), .Q(S[4]), .en(1'b1));  // open: Qn, preset, reset
  Multiplexer #(.enable("false")) multiplexer_6 (.in0(S[4]), .in1(B[5]), .out(multiplexer_6_out), .sel(Set));
  D_Flip_Flop d_ff_6 (.clk(Clk), .D(multiplexer_6_out), .Q(S[5]), .en(1'b1));  // open: Qn, preset, reset
  Multiplexer #(.enable("false")) multiplexer_7 (.in0(S[5]), .in1(B[6]), .out(multiplexer_7_out), .sel(Set));
  D_Flip_Flop d_ff_7 (.clk(Clk), .D(multiplexer_7_out), .Q(S[6]), .en(1'b1));  // open: Qn, preset, reset
  Multiplexer #(.enable("false")) multiplexer_8 (.in0(S[6]), .in1(B[7]), .out(multiplexer_8_out), .sel(Set));
  D_Flip_Flop d_ff_8 (.clk(Clk), .D(multiplexer_8_out), .Q(S[7]), .en(1'b1));  // open: Qn, preset, reset

  // Notes on the sheet:
  //   Descolamento à esquerda
endmodule

module desloc_right (
  input  [7:0] B,
  input  Clk,
  input  Set,
  output [7:0] S
);

  wire multiplexer_1_out, multiplexer_2_out, multiplexer_3_out, multiplexer_4_out, multiplexer_5_out,
       multiplexer_6_out, multiplexer_7_out, multiplexer_8_out;

  Multiplexer #(.enable("false")) multiplexer_1 (.in0(S[1]), .in1(B[0]), .out(multiplexer_1_out), .sel(Set));
  D_Flip_Flop d_ff_1 (.clk(Clk), .D(multiplexer_1_out), .Q(S[0]), .en(1'b1));  // open: Qn, preset, reset
  Multiplexer #(.enable("false")) multiplexer_2 (.in0(S[2]), .in1(B[1]), .out(multiplexer_2_out), .sel(Set));
  D_Flip_Flop d_ff_2 (.clk(Clk), .D(multiplexer_2_out), .Q(S[1]), .en(1'b1));  // open: Qn, preset, reset
  Multiplexer #(.enable("false")) multiplexer_3 (.in0(S[3]), .in1(B[2]), .out(multiplexer_3_out), .sel(Set));
  D_Flip_Flop d_ff_3 (.clk(Clk), .D(multiplexer_3_out), .Q(S[2]), .en(1'b1));  // open: Qn, preset, reset
  Multiplexer #(.enable("false")) multiplexer_4 (.in0(S[4]), .in1(B[3]), .out(multiplexer_4_out), .sel(Set));
  D_Flip_Flop d_ff_4 (.clk(Clk), .D(multiplexer_4_out), .Q(S[3]), .en(1'b1));  // open: Qn, preset, reset
  Multiplexer #(.enable("false")) multiplexer_5 (.in0(S[5]), .in1(B[4]), .out(multiplexer_5_out), .sel(Set));
  D_Flip_Flop d_ff_5 (.clk(Clk), .D(multiplexer_5_out), .Q(S[4]), .en(1'b1));  // open: Qn, preset, reset
  Multiplexer #(.enable("false")) multiplexer_6 (.in0(S[6]), .in1(B[5]), .out(multiplexer_6_out), .sel(Set));
  D_Flip_Flop d_ff_6 (.clk(Clk), .D(multiplexer_6_out), .Q(S[5]), .en(1'b1));  // open: Qn, preset, reset
  Multiplexer #(.enable("false")) multiplexer_7 (.in0(S[7]), .in1(B[6]), .out(multiplexer_7_out), .sel(Set));
  D_Flip_Flop d_ff_7 (.clk(Clk), .D(multiplexer_7_out), .Q(S[6]), .en(1'b1));  // open: Qn, preset, reset
  Multiplexer #(.enable("false")) multiplexer_8 (.in0(1'b0), .in1(B[7]), .out(multiplexer_8_out), .sel(Set));
  D_Flip_Flop d_ff_8 (.clk(Clk), .D(multiplexer_8_out), .Q(S[7]), .en(1'b1));  // open: Qn, preset, reset

  // Notes on the sheet:
  //   Descolamento à direita
endmodule

module ALU (
  input  Set,
  input  Clk,
  input  [7:0] A,
  input  [7:0] B,
  input  [3:0] Chave,
  output [7:0] \Saída 
);

  wire [7:0] adder_8bits_1_s, AND_out, desloc_left_1_s, desloc_right_1_s, multiplier_1_out, NAND_out,
       NOR_out, not_1_out, OR_out, subtractor_8bits_1_s, XNOR_out, XOR_out;

  Multiplier multiplier_1 (.a(A), .b(B), .out(multiplier_1_out));  // open: cin, cout
  assign AND_out = A & B;  // AND_Gate AND, 8 bits wide
  assign OR_out = A | B;  // OR_Gate OR, 8 bits wide
  assign not_1_out = ~B;  // NOT_Gate not_1, 8 bits wide
  desloc_left desloc_left_1 (.Clk(Clk), .Set(Set), .B(B), .S(desloc_left_1_s));
  desloc_right desloc_right_1 (.Clk(Clk), .Set(Set), .B(B), .S(desloc_right_1_s));
  subtractor_8bits subtractor_8bits_1 (.A(A), .B(B), .S(subtractor_8bits_1_s));
  adder_8bits adder_8bits_1 (.A(A), .B(B), .S(adder_8bits_1_s));
  assign XOR_out = A ^ B;  // XOR_Gate XOR, 8 bits wide
  assign NOR_out = ~(A | B);  // NOR_Gate NOR, 8 bits wide
  assign NAND_out = ~(A & B);  // NAND_Gate NAND, 8 bits wide
  assign XNOR_out = ~(A ^ B);  // XNOR_Gate XNOR, 8 bits wide
  Multiplexer #(.select(4), .width(8), .enable("false")) multiplexer_1 (
    .in2(NAND_out), .in4(AND_out), .in5(NOR_out), .in6(desloc_right_1_s), .in7(desloc_left_1_s),
    .in8(not_1_out), .in9(adder_8bits_1_s), .in10(subtractor_8bits_1_s), .in11(XNOR_out), .in12(OR_out),
    .in13(XOR_out), .in14(multiplier_1_out), .out(\Saída ), .sel(Chave));  // open: in0, in1, in3, in15

  // Notes on the sheet:
  //   Multiplicador
  //   NOT
  //   Seletora
endmodule
