// Logisim project circuito_relatorio_1.circ as structural Verilog: 6 circuits, main circuit half-adder
module half_adder (
  input  A,
  input  B,
  output S,
  output Cout
);

  xor xor_1 (S, A, B);
  and and_1 (Cout, A, B);
endmodule

module full_adder (
  input  A,
  input  B,
  input  Cin,
  output Soma,
  output Cin_2
);

  wire half_adder_1_cout, half_adder_1_s, half_adder_2_cout;

  half_adder half_adder_1 (.A(A), .B(B), .S(half_adder_1_s), .Cout(half_adder_1_cout));
  half_adder half_adder_2 (.A(half_adder_1_s), .B(Cin), .S(Soma), .Cout(half_adder_2_cout));
  or or_1 (Cin_2, half_adder_2_cout, half_adder_1_cout);
endmodule

module half_subtractor (
  input  A,
  input  B,
  output S,
  output Bout
);

  xnor xnor_1 (S, A, B);
  and and_1 (Bout, A, B);
endmodule

module full_subtractor (
  input  A,
  input  B,
  input  Bin,
  output S,
  output Bout
);

  wire half_subtractor_1_bout, half_subtractor_1_s, half_subtractor_2_bout;

  half_subtractor half_subtractor_1 (.A(A), .B(B), .S(half_subtractor_1_s), .Bout(half_subtractor_1_bout));
  half_subtractor half_subtractor_2 (.A(half_subtractor_1_s), .B(Bin), .S(S), .Bout(half_subtractor_2_bout));
  or or_1 (Bout, half_subtractor_2_bout, half_subtractor_1_bout);
endmodule

module questao_1 (
  input  A,
  input  B,
  input  in_3,
  input  in_4,
  input  A_2,
  input  S0,
  input  S1,
  input  B_2,
  output out_9,
  output out_10,
  output out_11,
  output out_12,
  output out_13,
  output out_14,
  output out_15
);

  wire demultiplexer_1_out0, demultiplexer_1_out1, demultiplexer_2_out0, demultiplexer_2_out1,
       half_adder_1_s, half_subtractor_1_s;

  Demultiplexer demultiplexer_1 (.out0(demultiplexer_1_out0), .out1(demultiplexer_1_out1), .in(A_2), .sel(S1), .en(S0));
  Demultiplexer demultiplexer_2 (.out0(demultiplexer_2_out0), .out1(demultiplexer_2_out1), .in(B_2), .sel(S1), .en(S0));
  half_adder half_adder_1 (.A(A), .B(B), .S(half_adder_1_s), .Cout(out_10));
  half_subtractor half_subtractor_1 (.A(A), .B(B), .S(half_subtractor_1_s), .Bout(out_11));
  half_adder half_adder_2 (.A(demultiplexer_1_out0), .B(demultiplexer_2_out0), .S(out_12), .Cout(out_13));
  half_subtractor half_subtractor_2 (.A(demultiplexer_1_out1), .B(demultiplexer_2_out1), .S(out_14), .Bout(out_15));
  Multiplexer multiplexer_1 (.in0(half_adder_1_s), .in1(half_subtractor_1_s), .out(out_9), .sel(in_3), .en(in_4));

  // Notes on the sheet:
  //   MUX
  //   DEMUX
endmodule

module questao_2 (
  input  A,
  input  B,
  input  In,
  input  C1,
  input  C0,
  input  A_2,
  input  B_2,
  input  In_2,
  input  S0,
  input  S1,
  output out_11,
  output out_12,
  output out_13,
  output out_14,
  output out_15,
  output out_16,
  output out_17
);

  wire demultiplexer_1_out0, demultiplexer_1_out1, demultiplexer_2_out0, demultiplexer_2_out1,
       demultiplexer_3_out0, demultiplexer_3_out1, full_adder_1_soma, full_subtractor_1_s;

  Demultiplexer demultiplexer_1 (.out0(demultiplexer_1_out0), .out1(demultiplexer_1_out1), .in(A_2), .sel(S1), .en(S0));
  Demultiplexer demultiplexer_2 (.out0(demultiplexer_2_out0), .out1(demultiplexer_2_out1), .in(B_2), .sel(S1), .en(S0));
  Demultiplexer demultiplexer_3 (
    .out0(demultiplexer_3_out0), .out1(demultiplexer_3_out1), .in(In_2), .sel(S1), .en(S0));
  full_adder full_adder_1 (.Soma(full_adder_1_soma), .Cin_2(out_11));  // open: A, B, Cin
  full_subtractor full_subtractor_1 (.S(full_subtractor_1_s), .Bout(out_13));  // open: A, B, Bin
  full_adder full_adder_2 (.Soma(out_14), .Cin_2(out_15));  // open: A, B, Cin
  full_subtractor full_subtractor_2 (.S(out_16), .Bout(out_17));  // open: A, B, Bin
  Multiplexer multiplexer_1 (.in0(full_adder_1_soma), .in1(full_subtractor_1_s), .out(out_12), .sel(C1), .en(C0));

  // Notes on the sheet:
  //   MUX
  //   DEMUX
endmodule
