// Logisim project circuito_relatorio_2.circ as structural Verilog: 3 circuits, main circuit complemento_2
module complemento_2 (
  input  [3:0] A,
  input  [3:0] B,
  input  Cin,
  output [3:0] S,
  output Cout
);

  wire full_adder_1_cin_2, full_adder_2_cin_2, full_adder_3_cin_2, multiplexer_1_out, multiplexer_2_out,
       multiplexer_3_out, multiplexer_4_out, not_1_out, not_2_out, not_3_out, not_4_out;

  not not_1 (not_1_out, B[0]);
  not not_2 (not_2_out, B[1]);
  not not_3 (not_3_out, B[2]);
  not not_4 (not_4_out, B[3]);
  Multiplexer #(.enable("false")) multiplexer_1 (.in0(not_1_out), .in1(B[0]), .out(multiplexer_1_out), .sel(Cin));
  Multiplexer #(.enable("false")) multiplexer_2 (.in0(not_2_out), .in1(B[1]), .out(multiplexer_2_out), .sel(Cin));
  Multiplexer #(.enable("false")) multiplexer_3 (.in0(not_3_out), .in1(B[2]), .out(multiplexer_3_out), .sel(Cin));
  Multiplexer #(.enable("false")) multiplexer_4 (.in0(not_4_out), .in1(B[3]), .out(multiplexer_4_out), .sel(Cin));
  full_adder full_adder_1 (.Soma(S[0]), .Cin_2(full_adder_1_cin_2));  // open: A, B, Cin
  full_adder full_adder_2 (.Soma(S[1]), .Cin_2(full_adder_2_cin_2));  // open: A, B, Cin
  full_adder full_adder_3 (.Soma(S[2]), .Cin_2(full_adder_3_cin_2));  // open: A, B, Cin
  full_adder full_adder_4 (.Soma(S[3]), .Cin_2(Cout));  // open: A, B, Cin
endmodule

module multiplicator (
  input  A1,
  input  A0,
  input  B1,
  input  B0,
  output P3,
  output P2,
  output P1,
  output P0
);

  wire and_1_out, and_2_out, and_3_out, half_adder_2_cout;

  and and_1 (and_1_out, A1, B1);
  half_adder half_adder_1 (.A(half_adder_2_cout), .B(and_1_out), .S(P2), .Cout(P3));
  and and_2 (and_2_out, A1, B0);
  and and_3 (and_3_out, A0, B1);
  and and_4 (P0, A0, B0);
  half_adder half_adder_2 (.A(and_3_out), .B(and_2_out), .S(P1), .Cout(half_adder_2_cout));
endmodule

module registrador (
  input  Clock,
  input  Carga,
  input  Clear,
  input  Enable,
  output [3:0] D,
  output [3:0] Q
);

  wire multiplexer_1_out, multiplexer_2_out, multiplexer_3_out, multiplexer_4_out;

  Multiplexer #(.enable("false")) multiplexer_1 (.in0(Q[0]), .in1(D[0]), .out(multiplexer_1_out), .sel(Carga));
  D_Flip_Flop d_ff_1 (.clk(Clock), .D(multiplexer_1_out), .Q(Q[0]), .en(Enable), .reset(Clear));  // open: Qn, preset
  D_Flip_Flop d_ff_2 (.clk(Clock), .D(multiplexer_2_out), .Q(Q[1]), .en(Enable), .reset(Clear));  // open: Qn, preset
  Multiplexer #(.enable("false")) multiplexer_2 (.in0(Q[1]), .in1(D[1]), .out(multiplexer_2_out), .sel(Carga));
  Multiplexer #(.enable("false")) multiplexer_3 (.in0(Q[2]), .in1(D[2]), .out(multiplexer_3_out), .sel(Carga));
  D_Flip_Flop d_ff_3 (.clk(Clock), .D(multiplexer_3_out), .Q(Q[2]), .en(Enable), .reset(Clear));  // open: Qn, preset
  Multiplexer #(.enable("false")) multiplexer_4 (.in0(Q[3]), .in1(D[3]), .out(multiplexer_4_out), .sel(Carga));
  D_Flip_Flop d_ff_4 (.clk(Clock), .D(multiplexer_4_out), .Q(Q[3]), .en(Enable), .reset(Clear));  // open: Qn, preset
endmodule
